# Fritzing sketch arduinocircuito (saved by Fritzing 0.9.3b)

parts:
  Componente2 = Arduino Mega 2560 (Rev3)
  Componente3 = Bluetooth HC-05 Macho

nets:
  N1: Componente2.D15/RX3, Componente3.TXD
  N2: Componente2.D14/TX3, Componente3.RXD
  5V: Componente2.5V, Componente3.VCC
  GND: Componente2.GND, Componente3.GND
